// Digital circuit Main.dig as structural Verilog
module Main (
  input  clk
);

  wire address_register_1_p3, address_register_2_p3, address_register_3_p3, address_register_4_p3,
       address_register_5_p3;
  wire [1:0] bus_control_p6, bus_control_p6_2, Stage_1_fetch_suppress;
  wire [2:0] address_register_5_p7, bus_control_p8;
  wire [3:0] address_register_3_p5, address_register_4_p5, address_register_5_p6, alu_1_p7, bus_control_p7,
       bus_control_p10, bus_control_p11;
  wire [6:0] alu_1_p2, bus_control_p4, bus_control_p9;
  wire [7:0] address_register_5_p5, bus_control_p3, Fetch_pipeout, gpr_1_lhs, gpr_1_rhs, memory_1_mem,
       Stage_1_pipeout, tranfer_register_1_main;
  wire [15:0] address_register_1_p1, address_register_1_p2;

  // Address_Register address_register_1: pin names not known; wires that end beside it: address_register_1_p1, address_register_1_p2, address_register_1_p3
  // Address_Register address_register_2: pin names not known; wires that end beside it: address_register_1_p1, address_register_1_p2, address_register_2_p3
  // Address_Register address_register_3: pin names not known; wires that end beside it: address_register_1_p1, address_register_1_p2, address_register_3_p3, address_register_3_p3, address_register_3_p5
  // Address_Register address_register_4: pin names not known; wires that end beside it: address_register_1_p1, address_register_1_p2, address_register_4_p3, address_register_4_p3, address_register_4_p5
  // Address_Register address_register_5: pin names not known; wires that end beside it: address_register_1_p1, address_register_1_p2, address_register_5_p3, address_register_5_p3, address_register_5_p5, address_register_5_p6, address_register_5_p7
  Tranfer_Register tranfer_register_1 (
    .MAIN(tranfer_register_1_main), .XFER(address_register_1_p1), .ADDR(address_register_1_p2),
    .Control(address_register_5_p5));
  Memory memory_1 (.ADDR(address_register_1_p2), .Control(address_register_5_p6), .MEM(memory_1_mem));
  // Bus_Control bus_control: pin names not known; wires that end beside it: address_register_1_p3, address_register_2_p3, bus_control_p3, bus_control_p4, {alu_1_p2[6], clk}, {bus_control_p6_2, bus_control_p6}, bus_control_p7, bus_control_p8, bus_control_p9, bus_control_p10, bus_control_p11
  GPR gpr_1 (.RHS(gpr_1_rhs), .LHS(gpr_1_lhs), .MAIN(tranfer_register_1_main), .Control(bus_control_p10));  // open: I
  GPR gpr_2 (.RHS(gpr_1_rhs), .LHS(gpr_1_lhs), .MAIN(tranfer_register_1_main), .Control(bus_control_p11));  // open: I
  GPR gpr_3 (
    .RHS(gpr_1_rhs), .LHS(gpr_1_lhs), .MAIN(tranfer_register_1_main), .Control(address_register_3_p5));  // open: I
  GPR gpr_4 (
    .RHS(gpr_1_rhs), .LHS(gpr_1_lhs), .MAIN(tranfer_register_1_main), .Control(address_register_4_p5));  // open: I
  Constant_Register constant_register_1 (
    .MEM(memory_1_mem), .MAIN(tranfer_register_1_main), .Control(address_register_5_p7));
  Memory_Bridge memory_bridge_1 (.MAIN(tranfer_register_1_main), .MEM(memory_1_mem), .Control(address_register_5_p6));
  // ALU alu_1: pin names not known; wires that end beside it: bus_control_p9[0], alu_1_p2[4:0], gpr_1_lhs, gpr_1_rhs, gpr_1_lhs, clk, alu_1_p7
  Stage_2 stage_2_1 (
    .Flags(alu_1_p2), .Clock(clk), .PipeIn(Stage_1_pipeout), .Main(bus_control_p3),
    .SPSIDI(bus_control_p6_2), .Addr(bus_control_p8), .Bus_Request(Stage_1_fetch_suppress[1]),
    .PCRA_Flip(alu_1_p2[5]));  // open: Break
  Stage_1 Stage_1 (
    .ALU_Bus(bus_control_p7), .ALU_Ops(alu_1_p7), .Xfer(bus_control_p4),
    .Fetch_suppress(Stage_1_fetch_suppress[0]), .Control(Stage_1_fetch_suppress), .PipeOut(Stage_1_pipeout),
    .Flags(alu_1_p2), .Clock(clk), .PipeIn(Fetch_pipeout));
  Fetch Fetch (
    .MEM(memory_1_mem), .Flags(alu_1_p2), .Clock(clk), .PCRA(bus_control_p6),
    .Control(Stage_1_fetch_suppress), .PipeOut(Fetch_pipeout));
  Button button_1 (.out(alu_1_p2[6]));
endmodule
